# Fritzing sketch PCBv11_final (saved by Fritzing 1.0.5)
circuit board: 6.83cm x 6.53cm
breadboards: 1

parts:
  J1 = female pin header, 15 pins [form="♀ (female)"]
  J3 = female pin header, 20 pins [form="♀ (female)"]
  J4 = female pin header, 20 pins [form="♀ (female)"]  # not connected
  JP1 = Header 4 [package=jst-4-pth]
  J2 = female pin header, 15 pins [form="♀ (female)"]
  JP2 = Header 2 [package=jst-2-pth-kit]

nets:
  N1: J1.pin6, JP1.1
  N2: J1.pin7, JP1.2
  N3: J1.pin15, J3.pin2, JP2.2
  N4: J3.pin3, JP1.4, J2.pin2, JP2.1
  N5: JP1.3, J2.pin1
